// Logisim project adder.circ as structural Verilog: 2 circuits, main circuit main
module main (
  input  sub,
  input  [15:0] A,
  input  [15:0] B,
  output [15:0] result,
  output ovf
);

  wire one_bit_adder_1_cout, one_bit_adder_2_cout, one_bit_adder_3_cout, one_bit_adder_4_cout,
       one_bit_adder_5_cout, one_bit_adder_6_cout, one_bit_adder_7_cout, one_bit_adder_8_cout,
       one_bit_adder_9_cout, one_bit_adder_10_cout, one_bit_adder_11_cout, one_bit_adder_12_cout,
       one_bit_adder_13_cout, one_bit_adder_14_cout, one_bit_adder_15_cout, one_bit_adder_16_cout, tunnel0,
       tunnel1, tunnel2, tunnel3, tunnel4, tunnel5, tunnel6, tunnel7, tunnel8, tunnel9, tunnel10, tunnel11,
       tunnel12, tunnel13, tunnel14, tunnel15;

  xor xor_1 (tunnel15, sub, B[15]);
  xor xor_2 (tunnel14, sub, B[14]);
  one_bit_adder one_bit_adder_1 (.Cin(sub), .a(tunnel0), .b(A[0]), .Cout(one_bit_adder_1_cout), .Sum(result[0]));
  xor xor_3 (tunnel13, sub, B[13]);
  one_bit_adder one_bit_adder_2 (
    .Cin(one_bit_adder_3_cout), .a(tunnel2), .b(A[2]), .Cout(one_bit_adder_2_cout), .Sum(result[2]));
  one_bit_adder one_bit_adder_3 (
    .Cin(one_bit_adder_1_cout), .a(tunnel1), .b(A[1]), .Cout(one_bit_adder_3_cout), .Sum(result[1]));
  xor xor_4 (tunnel12, sub, B[12]);
  xor xor_5 (tunnel12, sub, B[12]);
  one_bit_adder one_bit_adder_4 (
    .Cin(one_bit_adder_2_cout), .a(tunnel3), .b(A[3]), .Cout(one_bit_adder_4_cout), .Sum(result[3]));
  xor xor_6 (tunnel11, sub, B[11]);
  one_bit_adder one_bit_adder_5 (
    .Cin(one_bit_adder_4_cout), .a(tunnel4), .b(A[4]), .Cout(one_bit_adder_5_cout), .Sum(result[4]));
  xor xor_7 (tunnel10, sub, B[10]);
  one_bit_adder one_bit_adder_6 (
    .Cin(one_bit_adder_5_cout), .a(tunnel5), .b(A[5]), .Cout(one_bit_adder_6_cout), .Sum(result[5]));
  one_bit_adder one_bit_adder_7 (
    .Cin(one_bit_adder_6_cout), .a(tunnel6), .b(A[6]), .Cout(one_bit_adder_7_cout), .Sum(result[6]));
  xor xor_8 (tunnel9, sub, B[9]);
  one_bit_adder one_bit_adder_8 (
    .Cin(one_bit_adder_7_cout), .a(tunnel7), .b(A[7]), .Cout(one_bit_adder_8_cout), .Sum(result[7]));
  xor xor_9 (tunnel8, sub, B[8]);
  xor xor_10 (tunnel8, sub, B[8]);
  one_bit_adder one_bit_adder_9 (
    .Cin(one_bit_adder_8_cout), .a(tunnel8), .b(A[8]), .Cout(one_bit_adder_9_cout), .Sum(result[8]));
  xor xor_11 (tunnel7, sub, B[7]);
  one_bit_adder one_bit_adder_10 (
    .Cin(one_bit_adder_9_cout), .a(tunnel9), .b(A[9]), .Cout(one_bit_adder_10_cout), .Sum(result[9]));
  one_bit_adder one_bit_adder_11 (
    .Cin(one_bit_adder_10_cout), .a(tunnel10), .b(A[10]), .Cout(one_bit_adder_11_cout), .Sum(result[10]));
  xor xor_12 (tunnel6, sub, B[6]);
  one_bit_adder one_bit_adder_12 (
    .Cin(one_bit_adder_11_cout), .a(tunnel11), .b(A[11]), .Cout(one_bit_adder_12_cout), .Sum(result[11]));
  xor xor_13 (tunnel5, sub, B[5]);
  one_bit_adder one_bit_adder_13 (
    .Cin(one_bit_adder_12_cout), .a(tunnel12), .b(A[12]), .Cout(one_bit_adder_13_cout), .Sum(result[12]));
  xor xor_14 (tunnel4, sub, B[4]);
  xor xor_15 (tunnel4, sub, B[4]);
  one_bit_adder one_bit_adder_14 (
    .Cin(one_bit_adder_15_cout), .a(tunnel14), .b(A[14]), .Cout(one_bit_adder_14_cout), .Sum(result[14]));
  one_bit_adder one_bit_adder_15 (
    .Cin(one_bit_adder_13_cout), .a(tunnel13), .b(A[13]), .Cout(one_bit_adder_15_cout), .Sum(result[13]));
  xor xor_16 (tunnel3, sub, B[3]);
  one_bit_adder one_bit_adder_16 (
    .Cin(one_bit_adder_14_cout), .a(tunnel15), .b(A[15]), .Cout(one_bit_adder_16_cout), .Sum(result[15]));
  xor xor_17 (tunnel2, sub, B[2]);
  xor xor_18 (tunnel1, sub, B[1]);
  xor xor_19 (ovf, one_bit_adder_14_cout, one_bit_adder_16_cout);
  xor xor_20 (tunnel0, sub, B[0]);
  xor xor_21 (tunnel0, sub, B[0]);
endmodule

module one_bit_adder (
  input  Cin,
  input  a,
  input  b,
  output Sum,
  output Cout
);

  wire and_1_out, and_2_out, xor_1_out;

  and and_1 (and_1_out, b, a);
  xor xor_1 (xor_1_out, a, b);
  or or_1 (Cout, and_1_out, and_2_out);
  and and_2 (and_2_out, xor_1_out, Cin);
  xor xor_2 (Sum, Cin, xor_1_out);
endmodule
