// Logisim project fsm.circ as structural Verilog: 1 circuit, main circuit main
module main (
  input  in1,
  input  in2,
  output out
);

  wire and_1_out, and_2_out, and_3_out, and_5_out, and_6_out, clk_out, D0, D1, NOTin1, NOTin2, NOTQ0, NOTQ1,
       Q0, Q1;

  Clock clk (.out(clk_out));
  not not_1 (NOTin1, in1);
  not not_2 (NOTin2, in2);
  D_Flip_Flop D1Q1 (.D(D1), .clk(clk_out), .Q(Q1), .Qn(NOTQ1));  // open: preset, reset
  D_Flip_Flop D0Q0 (.D(D0), .clk(clk_out), .Q(Q0), .Qn(NOTQ0));  // open: preset, reset
  and and_1 (and_1_out, NOTQ1, Q0, NOTin1, in2);
  and and_2 (and_2_out, NOTQ1, Q0, in1, NOTin2);
  and and_3 (and_3_out, Q1, NOTQ0);
  or or_1 (D1, and_1_out, and_2_out, and_3_out);
  and and_4 (out, Q1, NOTQ0);
  and and_5 (and_5_out, NOTQ1, NOTQ0, NOTin1, in2);
  and and_6 (and_6_out, NOTQ1, NOTQ0, in1, NOTin2);
  or or_2 (D0, and_5_out, and_6_out);
endmodule
