// Logisim project hw4.circ as structural Verilog: 18 circuits, main circuit main
module main (
  input  reset
);

  wire ALUinB, and_1_out, and_2_out, BEQ, BLT, DMwe, EqualCheck, Falling, Input, JAL, JP, keyboard_1_avail,
       LessCheck, memory_latch_1_oe_latched, memory_latch_1_we_latched, or_1_out, or_2_out, Output, Rdst,
       Rising, Rwd, Rwe;
  wire [2:0] multiplexer_1_out, multiplexer_2_out, Optype;
  wire [6:0] keyboard_1_data;
  wire [11:0] Address;
  wire [15:0] bit_extender_1_out, Data_Memory_f2c9798d_dout, memory_latch_1_address_latched,
       memory_latch_1_data_in_latched, multiplexer_3_out, multiplexer_4_out, multiplexer_5_out,
       multiplexer_7_out, multiplexer_8_out, multiplexer_9_out, my_adder_2_result, my_alu_1_output, my_input,
       NextPC, PC, R1, R2;
  wire [15:12] Instruction_Memory_dce2b358_data;

  Clock clock_1 (.out(Rising));
  my_register u_PC (.data_in(multiplexer_8_out), .clk(Rising), .reset(reset), .write_enable(1'b1), .data_out(PC));
  not not_1 (Falling, Rising);
  my_adder my_adder_1 (.A(16'h1), .B(PC), .result(NextPC), .sub(1'b0));  // open: ovf
  ROM #(.addrWidth(16), .dataWidth(16)) Instruction_Memory_dce2b358 (
    .addr(PC), .data({Instruction_Memory_dce2b358_data, Address}));
  my_control my_control_1 (
    .opcode(Instruction_Memory_dce2b358_data), .optype(Optype), .BEQ(BEQ), .BLT(BLT), .JP(JP), .JAL(JAL),
    .ALUinB(ALUinB), .DMwe(DMwe), .Rwe(Rwe), .Rdst(Rdst), .Rwd(Rwd), .\output (Output), .\input (Input));
  Multiplexer #(.width(3), .enable("false")) multiplexer_1 (
    .in0(Address[8:6]), .in1(Address[5:3]), .out(multiplexer_1_out), .sel(Rdst));
  assign bit_extender_1_out = {{10{Address[5]}}, Address[5:0]};  // Bit_Extender bit_extender_1
  Keyboard keyboard_1 (.clk(Rising), .re(Input), .clr(reset), .avail(keyboard_1_avail), .data(keyboard_1_data));
  Multiplexer #(.width(3), .enable("false")) multiplexer_2 (
    .in0(multiplexer_1_out), .in1(3'b111), .out(multiplexer_2_out), .sel(JAL));
  Multiplexer #(.width(16), .enable("false")) multiplexer_3 (
    .in0(multiplexer_9_out), .in1(my_input), .out(multiplexer_3_out), .sel(Input));
  Multiplexer #(.width(16), .enable("false")) multiplexer_4 (
    .in0(multiplexer_3_out), .in1(NextPC), .out(multiplexer_4_out), .sel(JAL));
  RegisterFile my_regfile (
    .rd(multiplexer_2_out), .data_in(multiplexer_4_out), .clk(Falling), .reset(reset), .write_enable(Rwe),
    .rs1(Address[11:9]), .rs2(Address[8:6]), .rs1_contents(R1), .rs2_contents(R2));
  Multiplexer #(.width(16), .enable("false")) multiplexer_5 (
    .in0(R2), .in1(bit_extender_1_out), .out(multiplexer_5_out), .sel(ALUinB));
  equals_check equals_check_1 (.r1(R1), .r2(R2), .\output (EqualCheck));
  lessthan_check lessthan_check_1 (.r1(R1), .r2(R2), .\output (LessCheck));
  memory_latch memory_latch_1 (
    .address(my_alu_1_output), .WE(DMwe), .clk(Rising), .data_in(R2),
    .address_latched(memory_latch_1_address_latched), .WE_latched(memory_latch_1_we_latched),
    .OE_latched(memory_latch_1_oe_latched), .data_in_latched(memory_latch_1_data_in_latched));
  my_ALU my_alu_1 (.A(R1), .B(multiplexer_5_out), .shamt(Address[2:0]), .optype(Optype), .\output (my_alu_1_output));
  Multiplexer #(.width(16), .enable("false")) multiplexer_6 (
    .in0(16'h40), .in1({{9{1'b0}}, keyboard_1_data}), .out(my_input), .sel(keyboard_1_avail));
  RAM #(.addrWidth(16), .dataWidth(16), .trigger("high"), .databus("bibus")) Data_Memory_f2c9798d (
    .addr(memory_latch_1_address_latched), .we(memory_latch_1_we_latched), .oe(memory_latch_1_oe_latched),
    .din(memory_latch_1_data_in_latched), .dout(Data_Memory_f2c9798d_dout));
  Multiplexer #(.width(16), .enable("false")) multiplexer_7 (
    .in0(NextPC), .in1(my_adder_2_result), .out(multiplexer_7_out), .sel(or_1_out));
  my_adder my_adder_2 (.A(NextPC), .B(bit_extender_1_out), .result(my_adder_2_result), .sub(1'b0));  // open: ovf
  or or_1 (or_1_out, and_1_out, and_2_out);
  and and_1 (and_1_out, BEQ, EqualCheck);
  and and_2 (and_2_out, BLT, LessCheck);
  or or_2 (or_2_out, JP, JAL);
  Multiplexer #(.width(16), .enable("false")) multiplexer_8 (
    .in0(multiplexer_7_out), .in1({NextPC[15:12], Address}), .out(multiplexer_8_out), .sel(or_2_out));
  Multiplexer #(.width(16), .enable("false")) multiplexer_9 (
    .in0(my_alu_1_output), .in1(Data_Memory_f2c9798d_dout), .out(multiplexer_9_out), .sel(Rwd));
  TTY #(.rows(13), .cols(80), .trigger("falling")) tty_1 (.data(R1[6:0]), .clk(Falling), .we(Output), .clr(reset));

  // Other names for the same wires on the sheet: Immediate[5:0] = Address[5:0]; Shamt[2:0] = Address[2:0];
  //   Rd[2:0] = Address[5:3]; Rt[2:0] = Address[8:6]; Rs[2:0] = Address[11:9]

  // Notes on the sheet:
  //   contents of Instruction_Memory_dce2b358 (hex, n*v repeats v):
  //   7000 6083 60c4 6100 b825 6900 b825 6900 b821 6900 1880 18c1 6080 60c0 880 8c1 203f
endmodule

module my_register (
  input  [15:0] data_in,
  input  clk,
  input  reset,
  input  write_enable,
  output [15:0] data_out
);

  wire and_1_out;

  and and_1 (and_1_out, clk, write_enable);
  D_Flip_Flop d_ff_1 (.D(data_in[0]), .clk(and_1_out), .Q(data_out[0]), .reset(reset));  // open: Qn, preset
  D_Flip_Flop d_ff_2 (.D(data_in[1]), .clk(and_1_out), .Q(data_out[1]), .reset(reset));  // open: Qn, preset
  D_Flip_Flop d_ff_3 (.D(data_in[2]), .clk(and_1_out), .Q(data_out[2]), .reset(reset));  // open: Qn, preset
  D_Flip_Flop d_ff_4 (.D(data_in[3]), .clk(and_1_out), .Q(data_out[3]), .reset(reset));  // open: Qn, preset
  D_Flip_Flop d_ff_5 (.D(data_in[4]), .clk(and_1_out), .Q(data_out[4]), .reset(reset));  // open: Qn, preset
  D_Flip_Flop d_ff_6 (.D(data_in[5]), .clk(and_1_out), .Q(data_out[5]), .reset(reset));  // open: Qn, preset
  D_Flip_Flop d_ff_7 (.D(data_in[6]), .clk(and_1_out), .Q(data_out[6]), .reset(reset));  // open: Qn, preset
  D_Flip_Flop d_ff_8 (.D(data_in[7]), .clk(and_1_out), .Q(data_out[7]), .reset(reset));  // open: Qn, preset
  D_Flip_Flop d_ff_9 (.D(data_in[8]), .clk(and_1_out), .Q(data_out[8]), .reset(reset));  // open: Qn, preset
  D_Flip_Flop d_ff_10 (.D(data_in[9]), .clk(and_1_out), .Q(data_out[9]), .reset(reset));  // open: Qn, preset
  D_Flip_Flop d_ff_11 (.D(data_in[10]), .clk(and_1_out), .Q(data_out[10]), .reset(reset));  // open: Qn, preset
  D_Flip_Flop d_ff_12 (.D(data_in[11]), .clk(and_1_out), .Q(data_out[11]), .reset(reset));  // open: Qn, preset
  D_Flip_Flop d_ff_13 (.D(data_in[12]), .clk(and_1_out), .Q(data_out[12]), .reset(reset));  // open: Qn, preset
  D_Flip_Flop d_ff_14 (.D(data_in[13]), .clk(and_1_out), .Q(data_out[13]), .reset(reset));  // open: Qn, preset
  D_Flip_Flop d_ff_15 (.D(data_in[14]), .clk(and_1_out), .Q(data_out[14]), .reset(reset));  // open: Qn, preset
  D_Flip_Flop d_ff_16 (.D(data_in[15]), .clk(and_1_out), .Q(data_out[15]), .reset(reset));  // open: Qn, preset
endmodule

module RegisterFile (
  input  [2:0] rd,
  input  [15:0] data_in,
  input  clk,
  input  reset,
  input  write_enable,
  input  [2:0] rs1,
  input  [2:0] rs2,
  output [15:0] rs1_contents,
  output [15:0] rs2_contents
);

  wire decoder_1_out1, decoder_1_out2, decoder_1_out3, decoder_1_out4, decoder_1_out5, decoder_1_out6,
       decoder_1_out7;
  wire [15:0] my_register_1_data_out, my_register_2_data_out, my_register_3_data_out, my_register_4_data_out,
       my_register_5_data_out, my_register_6_data_out, my_register_7_data_out;

  Decoder #(.select(3)) decoder_1 (
    .out1(decoder_1_out1), .out2(decoder_1_out2), .out3(decoder_1_out3), .out4(decoder_1_out4),
    .out5(decoder_1_out5), .out6(decoder_1_out6), .out7(decoder_1_out7), .sel(rd), .en(write_enable));  // open: out0
  // Probe on my_register_1_data_out
  my_register my_register_1 (
    .data_in(data_in), .clk(clk), .reset(reset), .write_enable(decoder_1_out1),
    .data_out(my_register_1_data_out));
  // Probe on my_register_2_data_out
  my_register my_register_2 (
    .data_in(data_in), .clk(clk), .reset(reset), .write_enable(decoder_1_out2),
    .data_out(my_register_2_data_out));
  // Probe on my_register_3_data_out
  my_register my_register_3 (
    .data_in(data_in), .clk(clk), .reset(reset), .write_enable(decoder_1_out3),
    .data_out(my_register_3_data_out));
  // Probe on my_register_4_data_out
  my_register my_register_4 (
    .data_in(data_in), .clk(clk), .reset(reset), .write_enable(decoder_1_out4),
    .data_out(my_register_4_data_out));
  // Probe on my_register_5_data_out
  my_register my_register_5 (
    .data_in(data_in), .clk(clk), .reset(reset), .write_enable(decoder_1_out5),
    .data_out(my_register_5_data_out));
  // Probe on my_register_6_data_out
  my_register my_register_6 (
    .data_in(data_in), .clk(clk), .reset(reset), .write_enable(decoder_1_out6),
    .data_out(my_register_6_data_out));
  // Probe on my_register_7_data_out
  my_register my_register_7 (
    .data_in(data_in), .clk(clk), .reset(reset), .write_enable(decoder_1_out7),
    .data_out(my_register_7_data_out));
  // Probe on {16{1'b0}}
  Multiplexer #(.select(3), .width(16), .enable("false")) multiplexer_1 (
    .in0({16{1'b0}}), .in1(my_register_1_data_out), .in2(my_register_2_data_out),
    .in3(my_register_3_data_out), .in4(my_register_4_data_out), .in5(my_register_5_data_out),
    .in6(my_register_6_data_out), .in7(my_register_7_data_out), .out(rs1_contents), .sel(rs1));
  Multiplexer #(.select(3), .width(16), .enable("false")) multiplexer_2 (
    .in0({16{1'b0}}), .in1(my_register_1_data_out), .in2(my_register_2_data_out),
    .in3(my_register_3_data_out), .in4(my_register_4_data_out), .in5(my_register_5_data_out),
    .in6(my_register_6_data_out), .in7(my_register_7_data_out), .out(rs2_contents), .sel(rs2));
endmodule

module one_bit_adder (
  input  Cin,
  input  a,
  input  b,
  output Sum,
  output Cout
);

  wire and_1_out, and_2_out, xor_1_out;

  and and_1 (and_1_out, b, a);
  xor xor_1 (xor_1_out, a, b);
  or or_1 (Cout, and_1_out, and_2_out);
  and and_2 (and_2_out, xor_1_out, Cin);
  xor xor_2 (Sum, Cin, xor_1_out);
endmodule

module my_adder (
  input  sub,
  input  [15:0] A,
  input  [15:0] B,
  output [15:0] result,
  output ovf
);

  wire one_bit_adder_1_cout, one_bit_adder_2_cout, one_bit_adder_3_cout, one_bit_adder_4_cout,
       one_bit_adder_5_cout, one_bit_adder_6_cout, one_bit_adder_7_cout, one_bit_adder_8_cout,
       one_bit_adder_9_cout, one_bit_adder_10_cout, one_bit_adder_11_cout, one_bit_adder_12_cout,
       one_bit_adder_13_cout, one_bit_adder_14_cout, one_bit_adder_15_cout, one_bit_adder_16_cout, tunnel0,
       tunnel1, tunnel2, tunnel3, tunnel4, tunnel5, tunnel6, tunnel7, tunnel8, tunnel9, tunnel10, tunnel11,
       tunnel12, tunnel13, tunnel14, tunnel15;

  xor xor_1 (tunnel15, sub, B[15]);
  xor xor_2 (tunnel14, sub, B[14]);
  one_bit_adder one_bit_adder_1 (.Cin(sub), .a(tunnel0), .b(A[0]), .Cout(one_bit_adder_1_cout), .Sum(result[0]));
  xor xor_3 (tunnel13, sub, B[13]);
  one_bit_adder one_bit_adder_2 (
    .Cin(one_bit_adder_3_cout), .a(tunnel2), .b(A[2]), .Cout(one_bit_adder_2_cout), .Sum(result[2]));
  one_bit_adder one_bit_adder_3 (
    .Cin(one_bit_adder_1_cout), .a(tunnel1), .b(A[1]), .Cout(one_bit_adder_3_cout), .Sum(result[1]));
  xor xor_4 (tunnel12, sub, B[12]);
  xor xor_5 (tunnel12, sub, B[12]);
  one_bit_adder one_bit_adder_4 (
    .Cin(one_bit_adder_2_cout), .a(tunnel3), .b(A[3]), .Cout(one_bit_adder_4_cout), .Sum(result[3]));
  xor xor_6 (tunnel11, sub, B[11]);
  one_bit_adder one_bit_adder_5 (
    .Cin(one_bit_adder_4_cout), .a(tunnel4), .b(A[4]), .Cout(one_bit_adder_5_cout), .Sum(result[4]));
  xor xor_7 (tunnel10, sub, B[10]);
  one_bit_adder one_bit_adder_6 (
    .Cin(one_bit_adder_7_cout), .a(tunnel6), .b(A[6]), .Cout(one_bit_adder_6_cout), .Sum(result[6]));
  one_bit_adder one_bit_adder_7 (
    .Cin(one_bit_adder_5_cout), .a(tunnel5), .b(A[5]), .Cout(one_bit_adder_7_cout), .Sum(result[5]));
  xor xor_8 (tunnel9, sub, B[9]);
  one_bit_adder one_bit_adder_8 (
    .Cin(one_bit_adder_6_cout), .a(tunnel7), .b(A[7]), .Cout(one_bit_adder_8_cout), .Sum(result[7]));
  xor xor_9 (tunnel8, sub, B[8]);
  xor xor_10 (tunnel8, sub, B[8]);
  one_bit_adder one_bit_adder_9 (
    .Cin(one_bit_adder_8_cout), .a(tunnel8), .b(A[8]), .Cout(one_bit_adder_9_cout), .Sum(result[8]));
  xor xor_11 (tunnel7, sub, B[7]);
  one_bit_adder one_bit_adder_10 (
    .Cin(one_bit_adder_9_cout), .a(tunnel9), .b(A[9]), .Cout(one_bit_adder_10_cout), .Sum(result[9]));
  one_bit_adder one_bit_adder_11 (
    .Cin(one_bit_adder_10_cout), .a(tunnel10), .b(A[10]), .Cout(one_bit_adder_11_cout), .Sum(result[10]));
  xor xor_12 (tunnel6, sub, B[6]);
  one_bit_adder one_bit_adder_12 (
    .Cin(one_bit_adder_11_cout), .a(tunnel11), .b(A[11]), .Cout(one_bit_adder_12_cout), .Sum(result[11]));
  xor xor_13 (tunnel5, sub, B[5]);
  one_bit_adder one_bit_adder_13 (
    .Cin(one_bit_adder_12_cout), .a(tunnel12), .b(A[12]), .Cout(one_bit_adder_13_cout), .Sum(result[12]));
  xor xor_14 (tunnel4, sub, B[4]);
  xor xor_15 (tunnel4, sub, B[4]);
  one_bit_adder one_bit_adder_14 (
    .Cin(one_bit_adder_15_cout), .a(tunnel14), .b(A[14]), .Cout(one_bit_adder_14_cout), .Sum(result[14]));
  one_bit_adder one_bit_adder_15 (
    .Cin(one_bit_adder_13_cout), .a(tunnel13), .b(A[13]), .Cout(one_bit_adder_15_cout), .Sum(result[13]));
  xor xor_16 (tunnel3, sub, B[3]);
  one_bit_adder one_bit_adder_16 (
    .Cin(one_bit_adder_14_cout), .a(tunnel15), .b(A[15]), .Cout(one_bit_adder_16_cout), .Sum(result[15]));
  xor xor_17 (tunnel2, sub, B[2]);
  xor xor_18 (tunnel1, sub, B[1]);
  xor xor_19 (ovf, one_bit_adder_14_cout, one_bit_adder_16_cout);
  xor xor_20 (tunnel0, sub, B[0]);
  xor xor_21 (tunnel0, sub, B[0]);
endmodule

module leftshift1 (
  input  [15:0] \input ,
  output [15:0] \output 
);


  assign \output  = {\input [14:0], 1'b0};
endmodule

module leftshift2 (
  input  [15:0] \input ,
  output [15:0] \output 
);


  assign \output  = {\input [13:0], 2'b00};
endmodule

module leftshift4 (
  input  [15:0] \input ,
  output [15:0] \output 
);


  assign \output  = {\input [11:0], 4'b0000};
endmodule

module rightshift1 (
  input  [15:0] \input ,
  output [15:0] \output 
);


  assign \output  = {1'b0, \input [15:1]};
endmodule

module rightshift2 (
  input  [15:0] \input ,
  output [15:0] \output 
);


  assign \output  = {2'b00, \input [15:2]};
endmodule

module rightshift4 (
  input  [15:0] \input ,
  output [15:0] \output 
);


  assign \output  = {4'b0000, \input [15:4]};
endmodule

module rightshifter (
  input  [15:0] \input ,
  input  [2:0] shiftval,
  output [15:0] \output 
);

  wire [15:0] multiplexer_1_out, multiplexer_2_out, rightshift1_1_output, rightshift2_1_output,
       rightshift4_1_output;

  Multiplexer #(.width(16), .enable("false")) multiplexer_1 (
    .in0(\input ), .in1(rightshift1_1_output), .out(multiplexer_1_out), .sel(shiftval[0]));
  rightshift1 rightshift1_1 (.\input (\input ), .\output (rightshift1_1_output));
  Multiplexer #(.width(16), .enable("false")) multiplexer_2 (
    .in0(multiplexer_1_out), .in1(rightshift2_1_output), .out(multiplexer_2_out), .sel(shiftval[1]));
  rightshift2 rightshift2_1 (.\input (multiplexer_1_out), .\output (rightshift2_1_output));
  rightshift4 rightshift4_1 (.\input (multiplexer_2_out), .\output (rightshift4_1_output));
  Multiplexer #(.width(16), .enable("false")) multiplexer_3 (
    .in0(multiplexer_2_out), .in1(rightshift4_1_output), .out(\output ), .sel(shiftval[2]));
endmodule

module leftshifter (
  input  [15:0] \input ,
  input  [2:0] shiftval,
  output [15:0] \output 
);

  wire [15:0] leftshift1_1_output, leftshift2_1_output, leftshift4_1_output, multiplexer_1_out,
       multiplexer_2_out;

  Multiplexer #(.width(16), .enable("false")) multiplexer_1 (
    .in0(\input ), .in1(leftshift1_1_output), .out(multiplexer_1_out), .sel(shiftval[0]));
  leftshift1 leftshift1_1 (.\input (\input ), .\output (leftshift1_1_output));
  Multiplexer #(.width(16), .enable("false")) multiplexer_2 (
    .in0(multiplexer_1_out), .in1(leftshift2_1_output), .out(multiplexer_2_out), .sel(shiftval[1]));
  leftshift2 leftshift2_1 (.\input (multiplexer_1_out), .\output (leftshift2_1_output));
  leftshift4 leftshift4_1 (.\input (multiplexer_2_out), .\output (leftshift4_1_output));
  Multiplexer #(.width(16), .enable("false")) multiplexer_3 (
    .in0(multiplexer_2_out), .in1(leftshift4_1_output), .out(\output ), .sel(shiftval[2]));
endmodule

module my_ALU (
  input  [15:0] A,
  input  [15:0] B,
  input  [2:0] shamt,
  input  [2:0] optype,
  output [15:0] \output 
);

  wire [15:0] and_1_out, leftshifter_1_output, my_adder_1_result, my_adder_2_result, or_1_out,
       rightshifter_1_output;

  assign or_1_out = A | B;  // OR_Gate or_1, 16 bits wide
  assign and_1_out = A & B;  // AND_Gate and_1, 16 bits wide
  my_adder my_adder_1 (.A(A), .B(B), .result(my_adder_1_result), .sub(1'b0));  // open: ovf
  my_adder my_adder_2 (.A(A), .B(B), .result(my_adder_2_result), .sub(1'b1));  // open: ovf
  rightshifter rightshifter_1 (.\input (A), .shiftval(shamt), .\output (rightshifter_1_output));
  leftshifter leftshifter_1 (.\input (A), .shiftval(shamt), .\output (leftshifter_1_output));
  Multiplexer #(.select(3), .width(16), .enable("false")) multiplexer_1 (
    .in0(or_1_out), .in1(and_1_out), .in2(my_adder_1_result), .in3(my_adder_2_result),
    .in4(rightshifter_1_output), .in5(leftshifter_1_output), .out(\output ), .sel(optype));  // open: in6, in7
endmodule

module my_control (
  input  [3:0] opcode,
  output BLT,
  output JAL,
  output Rdst,
  output Rwd,
  output \output ,
  output \input ,
  output BEQ,
  output JP,
  output ALUinB,
  output Rwe,
  output DMwe,
  output [2:0] optype
);

  wire decoder_1_out0, decoder_1_out1, decoder_1_out2, decoder_1_out3, decoder_1_out4, decoder_1_out5,
       decoder_1_out6, decoder_1_out7, decoder_1_out8, decoder_1_out9, decoder_1_out10, decoder_1_out11,
       decoder_1_out12, decoder_1_out13, decoder_1_out14, decoder_1_out15;

  Decoder #(.select(4)) decoder_1 (
    .out0(decoder_1_out0), .out1(decoder_1_out1), .out2(decoder_1_out2), .out3(decoder_1_out3),
    .out4(decoder_1_out4), .out5(decoder_1_out5), .out6(decoder_1_out6), .out7(decoder_1_out7),
    .out8(decoder_1_out8), .out9(decoder_1_out9), .out10(decoder_1_out10), .out11(decoder_1_out11),
    .out12(decoder_1_out12), .out13(decoder_1_out13), .out14(decoder_1_out14), .out15(decoder_1_out15),
    .sel(opcode));  // open: en
  buf u_BLT (BLT, decoder_1_out3);  // OR_Gate
  buf u_BEQ (BEQ, decoder_1_out2);  // OR_Gate
  buf u_JAL (JAL, decoder_1_out13);  // OR_Gate
  buf u_JP (JP, decoder_1_out12);  // OR_Gate
  or u_ALUinB (ALUinB, decoder_1_out0, decoder_1_out1, decoder_1_out6, decoder_1_out9);
  buf u_DMwe (DMwe, decoder_1_out1);  // OR_Gate
  or u_Rwe (Rwe, decoder_1_out13, decoder_1_out10, decoder_1_out7, decoder_1_out0, decoder_1_out4, decoder_1_out15, decoder_1_out5, decoder_1_out6, decoder_1_out8, decoder_1_out11, decoder_1_out9);
  or u_Rdst (Rdst, decoder_1_out10, decoder_1_out4, decoder_1_out5, decoder_1_out15, decoder_1_out7, decoder_1_out8, decoder_1_out11);
  buf u_Rwd (Rwd, decoder_1_out0);  // OR_Gate
  buf u_output (\output , decoder_1_out14);  // OR_Gate
  or or_1 (optype[2], decoder_1_out11, decoder_1_out10);
  buf u_input (\input , decoder_1_out15);  // OR_Gate
  or or_2 (optype[1], decoder_1_out9, decoder_1_out8, decoder_1_out7, decoder_1_out6, decoder_1_out0, decoder_1_out1, decoder_1_out2, decoder_1_out3);
  or or_3 (optype[0], decoder_1_out2, decoder_1_out3, decoder_1_out5, decoder_1_out8, decoder_1_out9, decoder_1_out11);
endmodule

module memory_latch (
  input  [15:0] address,
  input  WE,
  input  clk,
  input  [15:0] data_in,
  output [15:0] address_latched,
  output WE_latched,
  output OE_latched,
  output [15:0] data_in_latched
);

  wire d_ff_1_q;
  wire [15:0] register_1_q;

  Register #(.width(16), .trigger("falling")) register_1 (
    .D(address), .en(WE), .clk(clk), .Q(register_1_q));  // open: clr
  D_Flip_Flop #(.trigger("falling")) d_ff_1 (.D(WE), .clk(clk), .Q(d_ff_1_q));  // open: Qn, preset, reset
  Register #(.width(16), .trigger("falling")) register_2 (
    .D(data_in), .en(WE), .clk(clk), .Q(data_in_latched));  // open: clr
  Multiplexer #(.width(16), .enable("false")) multiplexer_1 (
    .in0(address), .in1(register_1_q), .out(address_latched), .sel(d_ff_1_q));
  and and_1 (WE_latched, clk, d_ff_1_q);
  not not_1 (OE_latched, WE_latched);
endmodule

module equals_check (
  input  [15:0] r1,
  input  [15:0] r2,
  output \output 
);

  wire not_1_out, not_2_out, not_3_out, not_4_out, not_5_out, not_6_out, not_7_out, not_8_out, not_9_out,
       not_10_out, not_11_out, not_12_out, not_13_out, not_14_out, not_15_out, not_16_out;
  wire [15:0] my_adder_1_result;

  my_adder my_adder_1 (.A(r1), .B(r2), .result(my_adder_1_result), .sub(1'b1));  // open: ovf
  not not_1 (not_1_out, my_adder_1_result[0]);
  not not_2 (not_2_out, my_adder_1_result[1]);
  not not_3 (not_3_out, my_adder_1_result[2]);
  not not_4 (not_4_out, my_adder_1_result[15]);
  not not_5 (not_5_out, my_adder_1_result[3]);
  not not_6 (not_6_out, my_adder_1_result[4]);
  not not_7 (not_7_out, my_adder_1_result[5]);
  not not_8 (not_8_out, my_adder_1_result[12]);
  not not_9 (not_9_out, my_adder_1_result[13]);
  not not_10 (not_10_out, my_adder_1_result[14]);
  not not_11 (not_11_out, my_adder_1_result[6]);
  not not_12 (not_12_out, my_adder_1_result[7]);
  not not_13 (not_13_out, my_adder_1_result[8]);
  not not_14 (not_14_out, my_adder_1_result[9]);
  not not_15 (not_15_out, my_adder_1_result[10]);
  not not_16 (not_16_out, my_adder_1_result[11]);
  and and_1 (\output , not_1_out, not_2_out, not_3_out, not_5_out, not_6_out, not_7_out, not_11_out, not_12_out, not_13_out, not_14_out, not_15_out, not_16_out, not_8_out, not_9_out, not_10_out, not_4_out);
endmodule

module lessthan_check (
  input  [15:0] r1,
  input  [15:0] r2,
  output \output 
);

  wire [14:0] my_adder_1_result;

  my_adder my_adder_1 (.A(r1), .B(r2), .result({\output , my_adder_1_result}), .sub(1'b1));  // open: ovf
endmodule
